// Logisim project alu.circ as structural Verilog: 1 circuit, main circuit alu
module alu (
  input  [31:0] A,
  input  [31:0] B,
  input  [3:0] ALUSel,
  output [31:0] ALUResult
);

  wire SLT2;
  wire [4:0] bit_extender_1_out, bit_extender_2_out, bit_extender_5_out;
  wire [31:0] add0, AND7, bit_extender_8_out, MUL8, MULH9, OR6, SLL1, SRA13, SRT5, SUB12, XOR4;
  wire [63:0] bit_extender_3_out, bit_extender_4_out, bit_extender_6_out, bit_extender_7_out, MULHU11;

  Bit_Extender #(.in_width(32), .out_width(5), .\type ("input")) bit_extender_1 (
    .in(B), .out(bit_extender_1_out));  // open: extend
  Bit_Extender #(.in_width(32), .out_width(5), .\type ("input")) bit_extender_2 (
    .in(B), .out(bit_extender_2_out));  // open: extend
  assign bit_extender_3_out = {{32{B[31]}}, B};  // Bit_Extender bit_extender_3
  assign bit_extender_4_out = {{32{1'b0}}, B};  // Bit_Extender bit_extender_4
  Bit_Extender #(.in_width(32), .out_width(5), .\type ("input")) bit_extender_5 (
    .in(B), .out(bit_extender_5_out));  // open: extend
  assign bit_extender_6_out = {{32{A[31]}}, A};  // Bit_Extender bit_extender_6
  assign bit_extender_7_out = {{32{1'b0}}, A};  // Bit_Extender bit_extender_7
  Adder #(.width(32)) adder_1 (.a(A), .b(B), .out(add0));  // open: cin, cout
  Shifter #(.width(32)) shifter_1 (.in(A), .\dist (bit_extender_1_out), .out(SLL1));
  Comparator #(.width(32)) comparator_1 (.a(A), .b(B), .lt(SLT2));  // open: gt, eq
  assign XOR4 = A ^ B;  // XOR_Gate xor_1, 32 bits wide
  Shifter #(.shift("lr"), .width(32)) shifter_2 (.in(A), .\dist (bit_extender_2_out), .out(SRT5));
  assign OR6 = A | B;  // OR_Gate or_1, 32 bits wide
  assign AND7 = A & B;  // AND_Gate and_1, 32 bits wide
  Multiplier #(.width(64)) multiplier_1 (
    .a(bit_extender_6_out), .b(bit_extender_3_out), .out({MULH9, MUL8}));  // open: cin, cout
  Multiplier #(.width(64)) multiplier_2 (
    .a(bit_extender_7_out), .b(bit_extender_4_out), .out(MULHU11));  // open: cin, cout
  Subtractor #(.width(32)) subtractor_1 (.a(A), .b(B), .out(SUB12));  // open: bin, bout
  Shifter #(.shift("ar"), .width(32)) shifter_3 (.in(A), .\dist (bit_extender_5_out), .out(SRA13));
  assign bit_extender_8_out = {{31{1'b0}}, SLT2};  // Bit_Extender bit_extender_8
  Multiplexer #(.select(4), .width(32)) multiplexer_1 (
    .in0(add0), .in1(SLL1), .in2(bit_extender_8_out), .in4(XOR4), .in5(SRT5), .in6(OR6), .in7(AND7),
    .in8(MUL8), .in9(MULH9), .in11(MULHU11[63:32]), .in12(SUB12), .in13(SRA13), .in15(B), .out(ALUResult),
    .sel(ALUSel));  // open: in3, in10, in14

  // Other names for the same wires on the sheet: BSEL15[31:0] = B

  // Notes on the sheet:
  //   INPUTS to your circuit
  //   DON'T CHANGE THE LOCATIONS OF THE INPUTS AND OUTPUTS!
  //   OUTPUT from your circuit
endmodule
