// Logisim project control-logic.circ as structural Verilog: 1 circuit, main circuit control_logic
module control_logic (
  input  [31:0] Instruction,
  input  BrEq,
  input  BrLt,
  output PCSel,
  output RegWEn,
  output [2:0] ImmSel,
  output BrUn,
  output ASel,
  output BSel,
  output [3:0] ALUSel,
  output MemWEn,
  output [1:0] WBSel
);

  wire and_3_out, and_4_out, and_5_out, and_17_out, and_18_out, AUtype, bitselector_6_out, bitselector_7_out,
       bitselector_8_out, bitselector_9_out, bitselector_10_out, bitselector_11_out, bitselector_12_out,
       BSuccess, Btype, fc3eq5, funct3_0, funct3_1, funct3_2, funct7_0, funct7_5, Itype, JItype, Jtype,
       Ltype, LUtype, not_1_out, not_2_out, not_3_out, not_4_out, not_5_out, not_6_out, not_7_out, not_8_out,
       not_9_out, not_10_out, not_11_out, not_12_out, not_13_out, not_14_out, not_15_out, not_16_out,
       not_17_out, not_18_out, not_19_out, not_20_out, not_21_out, not_22_out, not_23_out, not_24_out,
       not_25_out, not_26_out, not_27_out, not_28_out, not_29_out, not_30_out, not_31_out, not_32_out,
       not_33_out, Rtype, Stype, xor_1_out, xor_2_out;
  wire [1:0] priority_encoder_1_out;
  wire [2:0] AU_ImmSel, J_ImmSel, JI_ImmSel, L_ImmSel, LU_ImmSel, S_ImmSel;
  wire [3:0] AU_ALUSel, J_ALUSel, JI_ALUSel, L_ALUSel, LU_ALUSel, priority_encoder_2_out, R_ALUSel, S_ALUSel;
  wire [3:3] I_ALUSel;

  // Probe on Instruction[31:25]
  BitSelector #(.width(3)) bitselector_1 (.in(Instruction[14:12]), .out(funct3_0), .sel(2'b00));
  // Probe on funct3_0
  BitSelector #(.width(3)) bitselector_2 (.in(Instruction[14:12]), .out(funct3_1), .sel(2'b01));
  // Probe on funct3_1
  BitSelector #(.width(3)) bitselector_3 (.in(Instruction[14:12]), .out(funct3_2), .sel(2'b10));
  // Probe on funct3_2
  BitSelector #(.width(7)) bitselector_4 (.in(Instruction[31:25]), .out(funct7_0), .sel(3'b000));
  // Probe on funct7_0
  BitSelector #(.width(7)) bitselector_5 (.in(Instruction[31:25]), .out(funct7_5), .sel(3'b101));
  // Probe on funct7_5
  not not_1 (not_1_out, funct3_1);
  // Probe on Instruction[6:0]
  and and_1 (fc3eq5, funct3_0, not_1_out, funct3_2);
  and and_2 (I_ALUSel[3], funct7_5, fc3eq5);
  not not_2 (not_2_out, funct7_0);
  and and_3 (and_3_out, not_2_out, not_3_out);
  not not_3 (not_3_out, funct7_5);
  and and_4 (and_4_out, funct7_0, not_4_out);
  not not_4 (not_4_out, funct7_5);
  not not_5 (not_5_out, funct7_0);
  and and_5 (and_5_out, not_5_out, funct7_5);
  Priority_Encoder #(.select_enc(2)) priority_encoder_1 (
    .in0(and_3_out), .in2(and_4_out), .in3(and_5_out), .out(priority_encoder_1_out));  // open: in1, gs, en_out, en_in
  // Probe on bitselector_6_out
  BitSelector #(.width(7)) bitselector_6 (.in(Instruction[6:0]), .out(bitselector_6_out), .sel(3'b000));
  // Probe on bitselector_7_out
  BitSelector #(.width(7)) bitselector_7 (.in(Instruction[6:0]), .out(bitselector_7_out), .sel(3'b001));
  // Probe on bitselector_8_out
  BitSelector #(.width(7)) bitselector_8 (.in(Instruction[6:0]), .out(bitselector_8_out), .sel(3'b010));
  // Probe on bitselector_9_out
  BitSelector #(.width(7)) bitselector_9 (.in(Instruction[6:0]), .out(bitselector_9_out), .sel(3'b011));
  // Probe on bitselector_10_out
  BitSelector #(.width(7)) bitselector_10 (.in(Instruction[6:0]), .out(bitselector_10_out), .sel(3'b100));
  // Probe on bitselector_11_out
  BitSelector #(.width(7)) bitselector_11 (.in(Instruction[6:0]), .out(bitselector_11_out), .sel(3'b101));
  // Probe on bitselector_12_out
  BitSelector #(.width(7)) bitselector_12 (.in(Instruction[6:0]), .out(bitselector_12_out), .sel(3'b110));
  assign R_ALUSel = {1'b0, Instruction[14:12]} | {priority_encoder_1_out, 2'b00};  // OR_Gate or_1, 4 bits wide
  not not_6 (not_6_out, bitselector_8_out);
  not not_7 (not_7_out, bitselector_9_out);
  not not_8 (not_8_out, bitselector_11_out);
  not not_9 (not_9_out, bitselector_12_out);
  not not_10 (not_10_out, bitselector_8_out);
  not not_11 (not_11_out, bitselector_9_out);
  not not_12 (not_12_out, bitselector_12_out);
  not not_13 (not_13_out, bitselector_8_out);
  not not_14 (not_14_out, bitselector_9_out);
  not not_15 (not_15_out, bitselector_10_out);
  not not_16 (not_16_out, bitselector_8_out);
  not not_17 (not_17_out, bitselector_9_out);
  not not_18 (not_18_out, bitselector_10_out);
  not not_19 (not_19_out, bitselector_11_out);
  not not_20 (not_20_out, bitselector_12_out);
  not not_21 (not_21_out, bitselector_8_out);
  not not_22 (not_22_out, bitselector_9_out);
  not not_23 (not_23_out, bitselector_10_out);
  not not_24 (not_24_out, bitselector_12_out);
  not not_25 (not_25_out, bitselector_10_out);
  not not_26 (not_26_out, bitselector_9_out);
  not not_27 (not_27_out, bitselector_10_out);
  not not_28 (not_28_out, bitselector_9_out);
  not not_29 (not_29_out, bitselector_11_out);
  not not_30 (not_30_out, bitselector_12_out);
  not not_31 (not_31_out, bitselector_9_out);
  not not_32 (not_32_out, bitselector_12_out);
  and and_6 (Itype, bitselector_6_out, bitselector_7_out, not_6_out, not_7_out, bitselector_10_out, not_8_out, not_9_out);
  and and_7 (Rtype, bitselector_6_out, bitselector_7_out, not_10_out, not_11_out, bitselector_10_out, bitselector_11_out, not_12_out);
  and and_8 (Btype, bitselector_6_out, bitselector_7_out, not_13_out, not_14_out, not_15_out, bitselector_11_out, bitselector_12_out);
  and and_9 (Ltype, bitselector_6_out, bitselector_7_out, not_16_out, not_17_out, not_18_out, not_19_out, not_20_out);
  and and_10 (Stype, bitselector_6_out, bitselector_7_out, not_21_out, not_22_out, not_23_out, bitselector_11_out, not_24_out);
  and and_11 (Jtype, bitselector_6_out, bitselector_7_out, bitselector_8_out, bitselector_9_out, not_25_out, bitselector_11_out, bitselector_12_out);
  and and_12 (JItype, bitselector_6_out, bitselector_7_out, bitselector_8_out, not_26_out, not_27_out, bitselector_11_out, bitselector_12_out);
  and and_13 (AUtype, bitselector_6_out, bitselector_7_out, bitselector_8_out, not_28_out, bitselector_10_out, not_29_out, not_30_out);
  and and_14 (LUtype, bitselector_6_out, bitselector_7_out, bitselector_8_out, not_31_out, bitselector_10_out, bitselector_11_out, not_32_out);
  // Probe on priority_encoder_2_out
  Priority_Encoder #(.select_enc(4)) priority_encoder_2 (
    .in0(Itype), .in1(Rtype), .in2(Btype), .in3(Ltype), .in4(Stype), .in5(Jtype), .in6(JItype), .in7(AUtype),
    .in8(LUtype), .out(priority_encoder_2_out));  // open: in9, in10, in11, in12, in13, in14, in15
  and and_15 (BrUn, funct3_1, Btype);
  and and_16 (ASel, Btype, BSuccess);
  xor xor_1 (xor_1_out, funct3_0, BrEq);
  not not_33 (not_33_out, funct3_2);
  xor xor_2 (xor_2_out, funct3_0, BrLt);
  and and_17 (and_17_out, xor_1_out, not_33_out);
  and and_18 (and_18_out, xor_2_out, funct3_2);
  or or_2 (BSel, ASel, Itype);
  or or_3 (RegWEn, Itype, Rtype);
  // Probe on ImmSel
  Multiplexer #(.select(4), .width(3)) multiplexer_1 (
    .in0(3'b000), .in1(3'b000), .in2(3'b010), .in3(L_ImmSel), .in4(S_ImmSel), .in5(J_ImmSel),
    .in6(JI_ImmSel), .in7(AU_ImmSel), .in8(LU_ImmSel), .out(ImmSel), .sel(priority_encoder_2_out));  // open: in9, in10, in11, in12, in13, in14, in15
  or or_4 (BSuccess, and_17_out, and_18_out);
  // Probe on ALUSel
  Multiplexer #(.select(4), .width(4)) multiplexer_2 (
    .in0({I_ALUSel[3], Instruction[14:12]}), .in1(R_ALUSel), .in2(4'b0000), .in3(L_ALUSel), .in4(S_ALUSel),
    .in5(J_ALUSel), .in6(JI_ALUSel), .in7(AU_ALUSel), .in8(LU_ALUSel), .out(ALUSel),
    .sel(priority_encoder_2_out));  // open: in9, in10, in11, in12, in13, in14, in15

  assign PCSel = ASel;

  // Other names for the same wires on the sheet: funct3[2:0] = Instruction[14:12]; I_ALUSel[2:0] = Instruction[14:12];
  //   funct7[6:0] = Instruction[31:25]

  // Notes on the sheet:
  //   INPUTS to your circuit
  //   DON'T CHANGE THE LOCATIONS OF THE INPUTS AND OUTPUTS!
  //   OUTPUT from your circuit
endmodule
