// Logisim project imm-gen.circ as structural Verilog: 1 circuit, main circuit imm_gen
module imm_gen (
  input  [31:0] Instruction,
  input  [2:0] ImmSel,
  output [31:0] Immediate
);

  wire and_1_out, and_2_out, and_3_out, and_4_out, and_5_out, bitselector_1_out, bitselector_2_out,
       bitselector_3_out, bitselector_4_out, not_1_out, not_2_out, not_3_out, not_4_out, not_5_out,
       not_6_out, not_7_out, not_8_out, not_9_out, not_10_out;
  wire [2:0] priority_encoder_1_out;
  wire [11:0] multiplexer_3_out;
  wire [19:0] multiplexer_2_out;
  wire [20:0] multiplexer_1_out;

  BitSelector #(.width(32)) bitselector_1 (.in(Instruction), .out(bitselector_1_out), .sel({5{1'b1}}));
  Multiplexer #(.width(21)) multiplexer_1 (
    .in0({21{1'b0}}), .in1({21{1'b1}}), .out(multiplexer_1_out), .sel(bitselector_1_out));
  Multiplexer #(.width(20)) multiplexer_2 (
    .in0({20{1'b0}}), .in1({20{1'b1}}), .out(multiplexer_2_out), .sel(bitselector_1_out));
  Multiplexer #(.width(12)) multiplexer_3 (
    .in0({12{1'b0}}), .in1({12{1'b1}}), .out(multiplexer_3_out), .sel(bitselector_1_out));
  BitSelector #(.width(3)) bitselector_2 (.in(ImmSel), .out(bitselector_2_out), .sel(2'b00));
  BitSelector #(.width(3)) bitselector_3 (.in(ImmSel), .out(bitselector_3_out), .sel(2'b01));
  BitSelector #(.width(3)) bitselector_4 (.in(ImmSel), .out(bitselector_4_out), .sel(2'b10));
  not not_1 (not_1_out, bitselector_2_out);
  not not_2 (not_2_out, bitselector_3_out);
  not not_3 (not_3_out, bitselector_4_out);
  not not_4 (not_4_out, bitselector_3_out);
  not not_5 (not_5_out, bitselector_4_out);
  not not_6 (not_6_out, bitselector_2_out);
  not not_7 (not_7_out, bitselector_4_out);
  not not_8 (not_8_out, bitselector_4_out);
  not not_9 (not_9_out, bitselector_2_out);
  not not_10 (not_10_out, bitselector_3_out);
  and and_1 (and_1_out, not_1_out, not_2_out, not_3_out);
  and and_2 (and_2_out, bitselector_2_out, not_4_out, not_5_out);
  and and_3 (and_3_out, not_6_out, bitselector_3_out, not_7_out);
  and and_4 (and_4_out, bitselector_2_out, bitselector_3_out, not_8_out);
  and and_5 (and_5_out, not_9_out, not_10_out, bitselector_4_out);
  Priority_Encoder priority_encoder_1 (
    .in0(and_1_out), .in1(and_2_out), .in2(and_3_out), .in3(and_4_out), .in4(and_5_out),
    .out(priority_encoder_1_out));  // open: in5, in6, in7, en_in, gs, en_out
  Multiplexer #(.select(3), .width(32)) multiplexer_4 (
    .in0({multiplexer_1_out, Instruction[30:20]}),
    .in1({multiplexer_1_out, Instruction[30:25], Instruction[11:7]}),
    .in2({multiplexer_2_out, Instruction[7], Instruction[30:25], Instruction[11:8], 1'b0}),
    .in3({Instruction[31:12], {12{1'b0}}}),
    .in4({multiplexer_3_out, Instruction[19:12], Instruction[20], Instruction[30:21], 1'b0}),
    .out(Immediate), .sel(priority_encoder_1_out));  // open: in5, in6, in7

  // Notes on the sheet:
  //   INPUTS to your circuit
  //   DON'T CHANGE THE LOCATIONS OF THE INPUTS AND OUTPUTS!
  //   OUTPUT from your circuit
endmodule
